# Fritzing sketch DESAIN RANGKAIAN UAS (saved by Fritzing 0.9.5d)

parts:
  Part1 = Soil Moisture Sensor
  U3 = ESP8266 NodeMCU LoLin base
  DHT1 = Humidity and Temperature Sensor DHT11
  LCM1602_IIC1 = LCM1602 IIC [part_number="LCM1602 IIC" chip_label="LCM1602 IIC" package="DIP (Dual Inline) [THT]"]
  LCD1 = LCD screen

nets:
  VCC: Part1.VCC, U3.3V1-0, U3.3V1-1, U3.3V1-2, U3.3V3-2, DHT1.Vcc, LCM1602_IIC1.VCC
  GND: Part1.GND, U3.GND1-0, U3.GND1-1, U3.GND1-2, U3.GND3-2, U3.GND8-10, DHT1.GND_2, LCM1602_IIC1.GND
  N1: Part1.SIG, U3.A0
  N2: U3.D0-0, U3.D0-3, LCM1602_IIC1.SDA
  N3: U3.D1-0, U3.D1-3, LCM1602_IIC1.SCL
  N4: U3.D2-0, U3.D2-3, DHT1.Data-signal
  VSS: LCM1602_IIC1.VSS, LCD1.VSS
  VDD: LCM1602_IIC1.VDD, LCD1.VDD
  N5: LCM1602_IIC1.V0, LCD1.V0
  N6: LCM1602_IIC1.RS, LCD1.RS
  N7: LCM1602_IIC1.RW, LCD1.R/W
  N8: LCM1602_IIC1.E, LCD1.E
  N9: LCM1602_IIC1.D0, LCD1.DB0
  N10: LCM1602_IIC1.D1, LCD1.DB1
  N11: LCM1602_IIC1.D2, LCD1.DB2
  N12: LCM1602_IIC1.D3, LCD1.DB3
  N13: LCM1602_IIC1.D4, LCD1.DB4
  N14: LCM1602_IIC1.D5, LCD1.DB5
  N15: LCM1602_IIC1.D6, LCD1.DB6
  N16: LCM1602_IIC1.D7, LCD1.DB7
  N17: LCM1602_IIC1.A, LCD1.LED+
  N18: LCM1602_IIC1.K, LCD1.LED-

notes:
  Sensor DHT11
  Sensor Soilmoisture
  ESP 8266
  LCD SCREEN

custom parts:
  ESP8266 NodeMCU LoLin base: ESP8266 based NodeMCU Base
  Humidity and Temperature Sensor DHT11: Digital relative humidity & temperature sensor DHT11
  LCM1602 IIC: I2C-Module to use a 1602 or 2004 LCD on with the wire.h libory Serial LCD Modul
